// Logisim project datapath.circ as structural Verilog: 1 circuit, main circuit main
module main (
);

  wire [15:0] Addr_Block_q, Reg_Block_q, Var_Block_q;

  Register #(.width(16), .trigger("rising")) Var_Block (.D(Var_Block_q), .Q(Var_Block_q));  // open: en, clk, clr
  Register #(.width(16), .trigger("rising")) Addr_Block (.D(Var_Block_q), .Q(Addr_Block_q));  // open: en, clk, clr
  Register #(.width(16), .trigger("rising")) PC (.D(Var_Block_q), .Q(Addr_Block_q));  // open: en, clk, clr
  Register #(.width(16), .trigger("rising")) IR (.D(Var_Block_q));  // open: en, Q, clk, clr
  Register #(.width(16), .trigger("rising")) Reg_Block (.D(Var_Block_q), .Q(Reg_Block_q));  // open: en, clk, clr
  RAM #(.addrWidth(16), .dataWidth(16), .bus("separate")) ram_1 (
    .addr(Addr_Block_q), .din(Var_Block_q), .data(Var_Block_q));  // open: str, sel, clk, ld, clr
  Register #(.width(16), .trigger("rising")) MDR (.D(Var_Block_q), .Q(Var_Block_q));  // open: en, clk, clr

  // Notes on the sheet:
  //   ALU
endmodule
